# Fritzing sketch PhaserInternals (saved by Fritzing 0.9.3b)
breadboards: 1

parts:
  Part1 = Arduino Uno (Rev3)
  J1 = Piezo Speaker
  R1 = Resistor [tolerance=±5% resistance=100 package="0603 [SMD]"]
  S1 = Momentary Switch [package=ksa_sealed_tac_switch]
  R2 = Resistor [tolerance=±5% resistance=220 package="0603 [SMD]"]
  LED1 = Super Flux LED blue [color=Blue]

nets:
  N1: Part1.D9_PWM, J1.pin2
  N2: Part1.D5_PWM, S1.1
  N3: Part1.D6_PWM, Part1.GND, R1.Pin_0, R2.Pin_1, LED1.cathode
  N4: Part1.3V3, S1.3
  N5: J1.pin1, R1.Pin_1
  N6: S1.2, R2.Pin_0
